// Logisim project Control_Unit.circ as structural Verilog: 1 circuit, main circuit Control Unit
module Control_Unit (
  input  [5:0] FuncCode,
  input  [5:0] OpCode,
  input  START,
  input  RESET,
  input  RamReady,
  output [17:0] SelectorCodes,
  output [2:0] FC_Selector,
  output [3:0] ALU_Op,
  output fetch,
  output reset_2,
  output rnd_kbd_Selector,
  output TTY_Enable,
  output ReadInstruction,
  output ChipSelect,
  output R_W,
  output halt
);

  wire clk, CS0, CS1, CS2, CS3, CS4, demultiplexer_1_out0, demultiplexer_2_out0, demultiplexer_3_out0,
       demultiplexer_4_out0, demultiplexer_5_out0, demultiplexer_6_out0, FETCH_q, IDLE_q, Load, Main,
       or_1_out, Pop, Push, ReadMemory_2_q, ReadMemory_q, Return, Store, WriteMemory_2_q, WriteMemory_q;

  Clock clock_1 (.out(clk));
  or or_1 (or_1_out, demultiplexer_1_out0, 1'b1);
  or or_2 (R_W, Push, Store);
  Demultiplexer #(.enable("false")) demultiplexer_1 (
    .out0(demultiplexer_1_out0), .out1(fetch), .in(IDLE_q), .sel(START));
  D_Flip_Flop IDLE (.clk(or_1_out), .D(clk), .Q(IDLE_q));  // open: Qn, preset, en, reset
  or or_3 (CS1, demultiplexer_2_out0, Pop);
  or or_4 (CS3, demultiplexer_4_out0, Load);
  or or_5 (CS4, demultiplexer_5_out0, Store);
  or or_6 (CS0, demultiplexer_6_out0, Return, fetch);
  D_Flip_Flop ReadMemory (.clk(CS1), .D(clk), .Q(ReadMemory_q));  // open: Qn, preset, en, reset
  D_Flip_Flop WriteMemory (.clk(CS2), .D(clk), .Q(WriteMemory_q));  // open: Qn, preset, en, reset
  or or_7 (CS2, demultiplexer_3_out0, Push);
  D_Flip_Flop ReadMemory_2 (.clk(CS3), .D(clk), .Q(ReadMemory_2_q));  // open: Qn, preset, en, reset
  D_Flip_Flop WriteMemory_2 (.clk(CS4), .D(clk), .Q(WriteMemory_2_q));  // open: Qn, preset, en, reset
  D_Flip_Flop u_FETCH (.clk(CS0), .D(clk), .Q(FETCH_q));  // open: Qn, preset, en, reset
  Demultiplexer #(.enable("false")) demultiplexer_2 (
    .out0(demultiplexer_2_out0), .out1(Return), .in(ReadMemory_q), .sel(RamReady));
  Demultiplexer #(.enable("false")) demultiplexer_3 (
    .out0(demultiplexer_3_out0), .out1(Return), .in(WriteMemory_q), .sel(RamReady));
  Demultiplexer #(.enable("false")) demultiplexer_4 (
    .out0(demultiplexer_4_out0), .out1(Return), .in(ReadMemory_2_q), .sel(RamReady));
  Demultiplexer #(.enable("false")) demultiplexer_5 (
    .out0(demultiplexer_5_out0), .out1(Return), .in(WriteMemory_2_q), .sel(RamReady));
  Demultiplexer #(.enable("false")) demultiplexer_6 (
    .out0(demultiplexer_6_out0), .out1(ReadInstruction), .in(FETCH_q), .sel(RamReady));
  Multiplexer #(.width(18), .enable("false")) multiplexer_1 (
    .in0(SelectorCodes), .in1(18'h10), .out(SelectorCodes), .sel(WriteMemory_q));
  Multiplexer #(.width(18), .enable("false")) multiplexer_2 (
    .in0(SelectorCodes), .in1(18'h20024), .out(SelectorCodes), .sel(Return));
  Multiplexer #(.width(18), .enable("false")) multiplexer_3 (
    .in0(SelectorCodes), .in1(18'h20021), .out(SelectorCodes), .sel(Return));
  Switcher_CU switcher_cu_1 (
    .kbd_rnd(rnd_kbd_Selector), .FuncCode(FuncCode), .OpCode(OpCode), .ALU_OP(ALU_Op),
    .TTY_Enable(TTY_Enable), .halt(halt), .SelectorCodes(SelectorCodes), .S_FC(FC_Selector), .pop(Pop),
    .push(Push), .load(Load), .store(Store), .Main_In(ReadInstruction), .Main_Out(Main));
  or or_8 (ChipSelect, CS4, CS3, CS2, CS1, CS0);

  assign reset_2 = RESET;

  // Other names for the same wires on the sheet: Chip_Select = ChipSelect; ReadIns = ReadInstruction; rst = RESET;
  //   Selector_Codes[17:0] = SelectorCodes

  // Notes on the sheet:
  //   Input_Output_Region
  //   Instruction-Lines
endmodule
